# Fritzing sketch lcd (saved by Fritzing 0.8.7b)

parts:
  LCD1 = LCD screen
  Raspberry_Pi_B_rev1 = Raspberry Pi B rev2
  VCC1 = Battery

nets:
  VSS: LCD1.VSS, LCD1.V0, LCD1.R/W, LCD1.LED-, Raspberry_Pi_B_rev1.GND, VCC1.-
  VDD: LCD1.VDD, LCD1.LED+, Raspberry_Pi_B_rev1.5V, VCC1.+
  N1: LCD1.E, Raspberry_Pi_B_rev1.GPIO_8
  N2: LCD1.DB4, Raspberry_Pi_B_rev1.GPIO_25
  N3: LCD1.DB5, Raspberry_Pi_B_rev1.GPIO_24
  N4: LCD1.DB6, Raspberry_Pi_B_rev1.GPIO_23
  N5: LCD1.DB7, Raspberry_Pi_B_rev1.GPIO_18
