# Fritzing sketch sensor (saved by Fritzing 0.8.7b)
breadboards: 1

parts:
  C1 = Electrolytic Capacitor [capacitance=1µF package="100 mil [THT, electrolytic]"]
  R1 = Resistor [tolerance=±5% resistance=2.2k package=THT]
  R2 = Photocell (LDR) [package=THT]
  Raspberry_Pi_B_rev1 = Raspberry Pi B rev2

nets:
  N1: C1.-, R2.pin_0, Raspberry_Pi_B_rev1.GPIO_4
  N2: C1.+, Raspberry_Pi_B_rev1.GND
  N3: R1.Pin_0, Raspberry_Pi_B_rev1.3V3
  N4: R1.Pin_1, R2.pin_1
